# Fritzing sketch fritzing_sketch (saved by Fritzing 0.9.3b)
circuit board: 8.46667cm x 5.64444cm
breadboards: 1

parts:
  5V_Bench_Power = Power plug
  Tactile_Switch = Momentary Switch [package=tactile-pth]
  4-Pin_Male_Header = Header 4 [package=1x04-smd]
  Microcontroller = atmega168a [package=dip]

nets:
  N1: 5V_Bench_Power.GND, Tactile_Switch.3, 4-Pin_Male_Header.1, Microcontroller.GND#7
  VCC: 5V_Bench_Power.VCC, 4-Pin_Male_Header.4, Microcontroller.VCC
  N2: Tactile_Switch.2, Microcontroller.PD2_(INT0)
  N3: 4-Pin_Male_Header.2, Microcontroller.PB3_(MOSI/OC2A)
  N4: 4-Pin_Male_Header.3, Microcontroller.PB5_(SCK)

custom parts:
  atmega168a: Atmel ATmega168a microcontroller. The hardware hacker favorite.
